# Fritzing sketch arduino_control_fan (saved by Fritzing 0.9.4)
circuit board: 8.46667cm x 5.64444cm
breadboards: 1

parts:
  ASIC_S9_Fan1 = Header 4 [package=molex-1x4_lock]
  ASIC_S9_Fan2 = Header 4 [package=molex-1x4_lock]
  Fan1 = Header 4 [package=molex-1x4_lock]
  Fan2 = Header 4 [package=molex-1x4_lock]
  Arduino_Fan1 = Header 4 [package=molex-1x4_lock]
  Arduino_Fan2 = Header 4 [package=molex-1x4_lock]
  R1 = Resistor [tolerance=±5% resistance=220 package=THT]
  R2 = Resistor [tolerance=±5% resistance=220 package=THT]
  R3 = Resistor [tolerance=±5% resistance=220 package=THT]
  R4 = Resistor [tolerance=±5% resistance=220 package=THT]

nets:
  N1: ASIC_S9_Fan1.1, ASIC_S9_Fan2.1, Fan1.1, Fan2.1, Arduino_Fan1.1, Arduino_Fan2.1, R2.Pin_0, R4.Pin_1
  N2: ASIC_S9_Fan1.2, Fan1.2, Arduino_Fan1.2
  N3: ASIC_S9_Fan1.3, R3.Pin_1, R4.Pin_0
  N4: ASIC_S9_Fan1.4, Fan1.4, Arduino_Fan1.4
  N5: ASIC_S9_Fan2.2, Fan2.2
  N6: ASIC_S9_Fan2.3, R1.Pin_0, R2.Pin_1
  N7: ASIC_S9_Fan2.4, Fan2.4, Arduino_Fan2.4
  N8: Arduino_Fan1.3, R3.Pin_0
  N9: Arduino_Fan2.3, R1.Pin_1
